# Fritzing sketch WC64 (saved by Fritzing 0.9.1b)
breadboards: 1

parts:
  part = Arduino Nano (Rev3.0)
  R1 = Resistor [tolerance=±5% resistance=1k package=THT]  # not connected
  C1 = Ceramic Capacitor [capacitance=10µF package="100 mil [THT, multilayer]"]
  S2 = Pushbutton [package=THT]
  R2 = Resistor [tolerance=±5% resistance=10k package=THT]
  R3 = Resistor [tolerance=±5% resistance=1k package=THT]  # not connected
  C2 = Ceramic Capacitor [capacitance=10µF package="100 mil [THT, multilayer]"]
  S3 = Pushbutton [package=THT]
  R4 = Resistor [tolerance=±5% resistance=10k package=THT]
  LDR = Photocell (LDR) [package=THT]
  R6 = Trimmer Potentiometer [maximum_resistance=10kΩ package=THT]
  8x8_Matrix_of_WS2812B = LED Dot Matrix 18mm (0.7 INCH)
  DS3231_AT24C32_IIC_High_Precision_Real_Time_Clock_Module_For_Arduino = female pin header, 6 pins [form="♀ (female)"]

nets:
  GND: part.GND, C1.0, C2.0, R6.leg2, 8x8_Matrix_of_WS2812B.Row_7
  N1: part.D2, C1.1
  N2: part.D3, C2.1
  N3: part.D4, 8x8_Matrix_of_WS2812B.Row_1
  5V: part.5V, R2.Pin_0, R4.Pin_0, LDR.pin_0, 8x8_Matrix_of_WS2812B.Column_1
  N4: part.A5, DS3231_AT24C32_IIC_High_Precision_Real_Time_Clock_Module_For_Arduino.pin1
  N5: part.A4, DS3231_AT24C32_IIC_High_Precision_Real_Time_Clock_Module_For_Arduino.pin2
  N6: S2.leg1, R2.Pin_1
  N7: S3.leg1, R4.Pin_1
  N8: LDR.pin_1, R6.wiper
